// Logisim project 1.circ as structural Verilog: 1 circuit, main circuit main
module main (
  input  in_1,
  input  in_2,
  input  in_3,
  input  in_4,
  input  in_5,
  input  in_6,
  input  in_7,
  input  in_8,
  input  in_9,
  input  in_10,
  input  in_11,
  input  in_12,
  input  in_13,
  input  in_14,
  input  in_15,
  input  in_16,
  input  in_17,
  input  in_18,
  input  in_19,
  input  in_20,
  input  in_21,
  input  in_22,
  input  in_23,
  input  in_24,
  input  in_25,
  input  in_26,
  input  in_27,
  input  in_28,
  input  in_29,
  input  in_30,
  input  in_31,
  input  in_32,
  input  in_33,
  input  in_34,
  input  in_35,
  input  in_36,
  input  in_37,
  input  in_38,
  input  in_39,
  input  in_40,
  input  in_41,
  input  in_42,
  input  in_43,
  input  in_44,
  input  in_45,
  input  in_46,
  input  in_47,
  input  in_48,
  input  in_49,
  input  in_50,
  input  in_51,
  input  in_52,
  input  in_53,
  input  in_54,
  input  in_55,
  input  in_56,
  input  in_57,
  input  in_58
);

  wire multiplexer_1_out, multiplexer_2_out, multiplexer_3_out, multiplexer_4_out, multiplexer_5_out,
       multiplexer_6_out, multiplexer_7_out, multiplexer_8_out, multiplexer_9_out, multiplexer_10_out,
       multiplexer_11_out, multiplexer_12_out, multiplexer_13_out, multiplexer_14_out, multiplexer_15_out,
       multiplexer_16_out, multiplexer_17_out, multiplexer_18_out, multiplexer_19_out, multiplexer_20_out,
       multiplexer_21_out, multiplexer_22_out, multiplexer_23_out, multiplexer_24_out, multiplexer_25_out,
       multiplexer_26_out, multiplexer_27_out, multiplexer_28_out, multiplexer_29_out, multiplexer_30_out,
       multiplexer_31_out, multiplexer_32_out, multiplexer_33_out, multiplexer_34_out, multiplexer_35_out,
       multiplexer_36_out, multiplexer_37_out, multiplexer_38_out, multiplexer_39_out, multiplexer_40_out,
       multiplexer_41_out, multiplexer_42_out, multiplexer_43_out, multiplexer_44_out, multiplexer_45_out,
       multiplexer_46_out, multiplexer_47_out, multiplexer_48_out, multiplexer_49_out, multiplexer_50_out,
       multiplexer_51_out, multiplexer_52_out, multiplexer_53_out, multiplexer_54_out, multiplexer_55_out,
       multiplexer_56_out, multiplexer_57_out, multiplexer_58_out, multiplexer_59_out, multiplexer_60_out,
       multiplexer_61_out, multiplexer_62_out, multiplexer_63_out, multiplexer_64_out, multiplexer_65_out,
       multiplexer_66_out, multiplexer_67_out, multiplexer_68_out, multiplexer_69_out, multiplexer_70_out,
       multiplexer_71_out, multiplexer_72_out, multiplexer_73_out, multiplexer_74_out, multiplexer_75_out,
       multiplexer_76_out, multiplexer_77_out, multiplexer_78_out, multiplexer_79_out, multiplexer_80_out,
       multiplexer_81_out, multiplexer_82_out, multiplexer_83_out, multiplexer_84_out, multiplexer_85_out,
       multiplexer_86_out, multiplexer_87_out, multiplexer_88_out, multiplexer_89_out, multiplexer_90_out,
       multiplexer_91_out, multiplexer_92_out, multiplexer_93_out, multiplexer_94_out, multiplexer_95_out,
       multiplexer_96_out, multiplexer_97_out, multiplexer_98_out, multiplexer_99_out, multiplexer_100_out,
       multiplexer_101_out, multiplexer_102_out, multiplexer_103_out, multiplexer_104_out,
       multiplexer_105_out, multiplexer_106_out, multiplexer_107_out, nand_1_out, nand_2_out, nand_3_out,
       nand_4_out, nand_5_out, nand_6_out, nand_7_out, nand_8_out, nand_9_out, nand_10_out, nand_11_out,
       nand_12_out, nand_13_out, nand_14_out, nand_15_out, nand_16_out, nand_17_out, nand_18_out,
       nand_19_out, nand_20_out, nand_21_out, nand_22_out, nand_23_out, nand_24_out, nand_25_out,
       nand_26_out, nand_27_out, nand_28_out, nand_29_out, nand_30_out, nand_31_out, nand_32_out,
       nand_33_out, nand_34_out, nand_35_out, nand_36_out, nand_37_out, nand_38_out, nand_39_out,
       nand_40_out, nand_41_out, nand_42_out, nand_43_out, not_1_out;

  not not_1 (not_1_out, in_1);
  nand nand_1 (nand_1_out, in_3, in_5);
  nand nand_2 (nand_2_out, in_17, in_19, in_21);
  nand nand_3 (nand_3_out, in_28, in_28);
  nand nand_4 (nand_4_out, in_35, in_35);
  nand nand_5 (nand_5_out, in_43, in_43);
  nand nand_6 (nand_6_out, in_7, nand_7_out);
  nand nand_7 (nand_7_out, nand_6_out, in_10);
  nand nand_8 (nand_8_out, in_11, in_13);
  nand nand_9 (nand_9_out, nand_8_out, nand_10_out);
  nand nand_10 (nand_10_out, nand_9_out, nand_11_out);
  nand nand_11 (nand_11_out, in_13, in_15);
  nand nand_12 (nand_12_out, in_26, nand_3_out);
  nand nand_13 (nand_13_out, nand_12_out, in_24, nand_14_out);
  nand nand_14 (nand_14_out, nand_13_out, in_31, nand_15_out);
  nand nand_15 (nand_15_out, nand_3_out, in_29);
  nand nand_16 (nand_16_out, nand_39_out, nand_4_out);
  nand nand_17 (nand_17_out, nand_16_out, in_34, nand_18_out);
  nand nand_18 (nand_18_out, nand_17_out, in_37, nand_19_out);
  nand nand_19 (nand_19_out, nand_4_out, nand_38_out);
  nand nand_20 (nand_20_out, nand_41_out, in_42, nand_5_out);
  nand nand_21 (nand_21_out, nand_20_out, in_40, nand_22_out);
  nand nand_22 (nand_22_out, nand_21_out, in_47, nand_23_out);
  nand nand_23 (nand_23_out, nand_5_out, in_45, nand_40_out);
  nand nand_24 (nand_24_out, nand_43_out, in_52, in_53);
  nand nand_25 (nand_25_out, nand_24_out, in_50, nand_26_out);
  nand nand_26 (nand_26_out, nand_25_out, in_57, nand_27_out);
  nand nand_27 (nand_27_out, in_53, in_55, nand_42_out);
  nand nand_28 (nand_28_out, in_28, nand_13_out);
  nand nand_29 (nand_29_out, nand_14_out, in_28);
  nand nand_30 (nand_30_out, in_35, nand_17_out);
  nand nand_31 (nand_31_out, nand_18_out, in_35);
  nand nand_32 (nand_32_out, in_43, nand_21_out);
  nand nand_33 (nand_33_out, nand_22_out, in_43);
  nand nand_34 (nand_34_out, nand_24_out, nand_27_out, nand_25_out);
  nand nand_35 (nand_35_out, nand_26_out, nand_27_out, nand_24_out);
  nand nand_36 (nand_36_out, nand_28_out, in_24, nand_37_out);
  nand nand_37 (nand_37_out, nand_36_out, in_31, nand_29_out);
  nand nand_38 (nand_38_out, nand_30_out, in_34, nand_39_out);
  nand nand_39 (nand_39_out, nand_38_out, in_37, nand_31_out);
  nand nand_40 (nand_40_out, nand_32_out, in_40, nand_41_out);
  nand nand_41 (nand_41_out, nand_40_out, in_47, nand_33_out);
  nand nand_42 (nand_42_out, nand_34_out, in_50, nand_43_out);
  nand nand_43 (nand_43_out, nand_42_out, in_57, nand_35_out);
  Multiplexer #(.disabled(0), .enable("false")) multiplexer_1 (
    .in0(1'b1), .in1(1'b0), .out(multiplexer_1_out), .sel(in_2));
  Multiplexer #(.disabled(0), .enable("false")) multiplexer_2 (
    .in0(in_6), .in1(in_4), .out(multiplexer_2_out), .sel(in_6));
  Multiplexer #(.disabled(0), .enable("false")) multiplexer_3 (
    .in0(1'b1), .in1(1'b0), .out(multiplexer_3_out), .sel(multiplexer_2_out));
  Multiplexer #(.disabled(0), .enable("false")) multiplexer_4 (
    .in0(1'b0), .in1(multiplexer_6_out), .out(multiplexer_4_out), .sel(in_8));
  Multiplexer #(.disabled(0), .enable("false")) multiplexer_5 (
    .in0(1'b1), .in1(1'b0), .out(multiplexer_5_out), .sel(multiplexer_4_out));
  Multiplexer #(.disabled(0), .enable("false")) multiplexer_6 (
    .in0(1'b1), .in1(1'b0), .out(multiplexer_6_out), .sel(multiplexer_7_out));
  Multiplexer #(.disabled(0), .enable("false")) multiplexer_7 (
    .in0(1'b0), .in1(multiplexer_5_out), .out(multiplexer_7_out), .sel(in_9));
  Multiplexer #(.disabled(0), .enable("false")) multiplexer_8 (
    .in0(1'b0), .in1(in_12), .out(multiplexer_8_out), .sel(in_14));
  Multiplexer #(.disabled(0), .enable("false")) multiplexer_9 (
    .in0(1'b1), .in1(1'b0), .out(multiplexer_9_out), .sel(multiplexer_8_out));
  Multiplexer #(.disabled(0), .enable("false")) multiplexer_10 (
    .in0(1'b0), .in1(in_16), .out(multiplexer_10_out), .sel(in_14));
  Multiplexer #(.disabled(0), .enable("false")) multiplexer_11 (
    .in0(1'b1), .in1(1'b0), .out(multiplexer_11_out), .sel(multiplexer_10_out));
  Multiplexer #(.disabled(0), .enable("false")) multiplexer_12 (
    .in0(1'b0), .in1(in_18), .out(multiplexer_12_out), .sel(in_20));
  Multiplexer #(.disabled(0), .enable("false")) multiplexer_13 (
    .in0(1'b0), .in1(in_25), .out(multiplexer_13_out), .sel(multiplexer_14_out));
  Multiplexer #(.disabled(0), .enable("false")) multiplexer_14 (
    .in0(1'b1), .in1(1'b0), .out(multiplexer_14_out), .sel(in_27));
  Multiplexer #(.disabled(0), .enable("false")) multiplexer_15 (
    .in0(1'b0), .in1(in_30), .out(multiplexer_15_out), .sel(multiplexer_14_out));
  Multiplexer #(.disabled(0), .enable("false")) multiplexer_16 (
    .in0(1'b0), .in1(multiplexer_95_out), .out(multiplexer_16_out), .sel(multiplexer_17_out));
  Multiplexer #(.disabled(0), .enable("false")) multiplexer_17 (
    .in0(1'b1), .in1(1'b0), .out(multiplexer_17_out), .sel(in_36));
  Multiplexer #(.disabled(0), .enable("false")) multiplexer_18 (
    .in0(1'b0), .in1(multiplexer_92_out), .out(multiplexer_18_out), .sel(multiplexer_17_out));
  Multiplexer #(.disabled(0), .enable("false")) multiplexer_19 (
    .in0(1'b1), .in1(1'b0), .out(multiplexer_19_out), .sel(in_44));
  Multiplexer #(.disabled(0), .enable("false")) multiplexer_20 (
    .in0(1'b0), .in1(multiplexer_41_out), .out(multiplexer_20_out), .sel(multiplexer_9_out));
  Multiplexer #(.disabled(0), .enable("false")) multiplexer_21 (
    .in0(1'b0), .in1(multiplexer_40_out), .out(multiplexer_21_out), .sel(multiplexer_11_out));
  Multiplexer #(.disabled(0), .enable("false")) multiplexer_22 (
    .in0(1'b0), .in1(multiplexer_12_out), .out(multiplexer_22_out), .sel(in_22));
  Multiplexer #(.disabled(0), .enable("false")) multiplexer_23 (
    .in0(1'b0), .in1(1'b1), .out(multiplexer_23_out), .sel(multiplexer_22_out));
  Multiplexer #(.disabled(0), .enable("false")) multiplexer_24 (
    .in0(1'b1), .in1(1'b0), .out(multiplexer_24_out), .sel(multiplexer_13_out));
  Multiplexer #(.disabled(0), .enable("false")) multiplexer_25 (
    .in0(1'b1), .in1(1'b0), .out(multiplexer_25_out), .sel(multiplexer_15_out));
  Multiplexer #(.disabled(0), .enable("false")) multiplexer_26 (
    .in0(1'b1), .in1(1'b0), .out(multiplexer_26_out), .sel(multiplexer_16_out));
  Multiplexer #(.disabled(0), .enable("false")) multiplexer_27 (
    .in0(1'b1), .in1(1'b0), .out(multiplexer_27_out), .sel(multiplexer_18_out));
  Multiplexer #(.disabled(0), .enable("false")) multiplexer_28 (
    .in0(1'b0), .in1(multiplexer_29_out), .out(multiplexer_28_out), .sel(multiplexer_19_out));
  Multiplexer #(.disabled(0), .enable("false")) multiplexer_29 (
    .in0(1'b0), .in1(multiplexer_101_out), .out(multiplexer_29_out), .sel(in_41));
  Multiplexer #(.disabled(0), .enable("false")) multiplexer_30 (
    .in0(1'b1), .in1(1'b0), .out(multiplexer_30_out), .sel(multiplexer_28_out));
  Multiplexer #(.disabled(0), .enable("false")) multiplexer_31 (
    .in0(1'b0), .in1(multiplexer_32_out), .out(multiplexer_31_out), .sel(multiplexer_19_out));
  Multiplexer #(.disabled(0), .enable("false")) multiplexer_32 (
    .in0(1'b0), .in1(multiplexer_98_out), .out(multiplexer_32_out), .sel(in_46));
  Multiplexer #(.disabled(0), .enable("false")) multiplexer_33 (
    .in0(1'b1), .in1(1'b0), .out(multiplexer_33_out), .sel(multiplexer_31_out));
  Multiplexer #(.disabled(0), .enable("false")) multiplexer_34 (
    .in0(1'b0), .in1(multiplexer_35_out), .out(multiplexer_34_out), .sel(in_54));
  Multiplexer #(.disabled(0), .enable("false")) multiplexer_35 (
    .in0(1'b0), .in1(multiplexer_107_out), .out(multiplexer_35_out), .sel(in_51));
  Multiplexer #(.disabled(0), .enable("false")) multiplexer_36 (
    .in0(1'b1), .in1(1'b0), .out(multiplexer_36_out), .sel(multiplexer_34_out));
  Multiplexer #(.disabled(0), .enable("false")) multiplexer_37 (
    .in0(1'b0), .in1(multiplexer_38_out), .out(multiplexer_37_out), .sel(in_54));
  Multiplexer #(.disabled(0), .enable("false")) multiplexer_38 (
    .in0(1'b0), .in1(multiplexer_104_out), .out(multiplexer_38_out), .sel(in_56));
  Multiplexer #(.disabled(0), .enable("false")) multiplexer_39 (
    .in0(1'b1), .in1(1'b0), .out(multiplexer_39_out), .sel(multiplexer_37_out));
  Multiplexer #(.disabled(0), .enable("false")) multiplexer_40 (
    .in0(1'b1), .in1(1'b0), .out(multiplexer_40_out), .sel(multiplexer_20_out));
  Multiplexer #(.disabled(0), .enable("false")) multiplexer_41 (
    .in0(1'b1), .in1(1'b0), .out(multiplexer_41_out), .sel(multiplexer_21_out));
  Multiplexer #(.disabled(0), .enable("false")) multiplexer_42 (
    .in0(1'b0), .in1(multiplexer_43_out), .out(multiplexer_42_out), .sel(in_23));
  Multiplexer #(.disabled(0), .enable("false")) multiplexer_43 (
    .in0(1'b0), .in1(multiplexer_55_out), .out(multiplexer_43_out), .sel(multiplexer_24_out));
  Multiplexer #(.disabled(0), .enable("false")) multiplexer_44 (
    .in0(1'b0), .in1(multiplexer_45_out), .out(multiplexer_44_out), .sel(in_32));
  Multiplexer #(.disabled(0), .enable("false")) multiplexer_45 (
    .in0(1'b0), .in1(multiplexer_54_out), .out(multiplexer_45_out), .sel(multiplexer_25_out));
  Multiplexer #(.disabled(0), .enable("false")) multiplexer_46 (
    .in0(1'b0), .in1(multiplexer_47_out), .out(multiplexer_46_out), .sel(in_33));
  Multiplexer #(.disabled(0), .enable("false")) multiplexer_47 (
    .in0(1'b0), .in1(multiplexer_57_out), .out(multiplexer_47_out), .sel(multiplexer_26_out));
  Multiplexer #(.disabled(0), .enable("false")) multiplexer_48 (
    .in0(1'b0), .in1(multiplexer_49_out), .out(multiplexer_48_out), .sel(in_38));
  Multiplexer #(.disabled(0), .enable("false")) multiplexer_49 (
    .in0(1'b0), .in1(multiplexer_56_out), .out(multiplexer_49_out), .sel(multiplexer_27_out));
  Multiplexer #(.disabled(0), .enable("false")) multiplexer_50 (
    .in0(1'b0), .in1(multiplexer_61_out), .out(multiplexer_50_out), .sel(multiplexer_30_out));
  Multiplexer #(.disabled(0), .enable("false")) multiplexer_51 (
    .in0(1'b0), .in1(multiplexer_59_out), .out(multiplexer_51_out), .sel(multiplexer_33_out));
  Multiplexer #(.disabled(0), .enable("false")) multiplexer_52 (
    .in0(1'b0), .in1(multiplexer_65_out), .out(multiplexer_52_out), .sel(multiplexer_36_out));
  Multiplexer #(.disabled(0), .enable("false")) multiplexer_53 (
    .in0(1'b0), .in1(multiplexer_63_out), .out(multiplexer_53_out), .sel(multiplexer_39_out));
  Multiplexer #(.disabled(0), .enable("false")) multiplexer_54 (
    .in0(1'b1), .in1(1'b0), .out(multiplexer_54_out), .sel(multiplexer_42_out));
  Multiplexer #(.disabled(0), .enable("false")) multiplexer_55 (
    .in0(1'b1), .in1(1'b0), .out(multiplexer_55_out), .sel(multiplexer_44_out));
  Multiplexer #(.disabled(0), .enable("false")) multiplexer_56 (
    .in0(1'b1), .in1(1'b0), .out(multiplexer_56_out), .sel(multiplexer_46_out));
  Multiplexer #(.disabled(0), .enable("false")) multiplexer_57 (
    .in0(1'b1), .in1(1'b0), .out(multiplexer_57_out), .sel(multiplexer_48_out));
  Multiplexer #(.disabled(0), .enable("false")) multiplexer_58 (
    .in0(1'b0), .in1(multiplexer_50_out), .out(multiplexer_58_out), .sel(in_39));
  Multiplexer #(.disabled(0), .enable("false")) multiplexer_59 (
    .in0(1'b1), .in1(1'b0), .out(multiplexer_59_out), .sel(multiplexer_58_out));
  Multiplexer #(.disabled(0), .enable("false")) multiplexer_60 (
    .in0(1'b0), .in1(multiplexer_51_out), .out(multiplexer_60_out), .sel(in_48));
  Multiplexer #(.disabled(0), .enable("false")) multiplexer_61 (
    .in0(1'b1), .in1(1'b0), .out(multiplexer_61_out), .sel(multiplexer_60_out));
  Multiplexer #(.disabled(0), .enable("false")) multiplexer_62 (
    .in0(1'b0), .in1(multiplexer_52_out), .out(multiplexer_62_out), .sel(in_49));
  Multiplexer #(.disabled(0), .enable("false")) multiplexer_63 (
    .in0(1'b1), .in1(1'b0), .out(multiplexer_63_out), .sel(multiplexer_62_out));
  Multiplexer #(.disabled(0), .enable("false")) multiplexer_64 (
    .in0(1'b0), .in1(multiplexer_53_out), .out(multiplexer_64_out), .sel(in_58));
  Multiplexer #(.disabled(0), .enable("false")) multiplexer_65 (
    .in0(1'b1), .in1(1'b0), .out(multiplexer_65_out), .sel(multiplexer_64_out));
  Multiplexer #(.disabled(0), .enable("false")) multiplexer_66 (
    .in0(1'b0), .in1(multiplexer_54_out), .out(multiplexer_66_out), .sel(in_27));
  Multiplexer #(.disabled(0), .enable("false")) multiplexer_67 (
    .in0(1'b1), .in1(1'b0), .out(multiplexer_67_out), .sel(multiplexer_66_out));
  Multiplexer #(.disabled(0), .enable("false")) multiplexer_68 (
    .in0(1'b0), .in1(multiplexer_55_out), .out(multiplexer_68_out), .sel(in_27));
  Multiplexer #(.disabled(0), .enable("false")) multiplexer_69 (
    .in0(1'b1), .in1(1'b0), .out(multiplexer_69_out), .sel(multiplexer_68_out));
  Multiplexer #(.disabled(0), .enable("false")) multiplexer_70 (
    .in0(1'b0), .in1(multiplexer_56_out), .out(multiplexer_70_out), .sel(in_36));
  Multiplexer #(.disabled(0), .enable("false")) multiplexer_71 (
    .in0(1'b1), .in1(1'b0), .out(multiplexer_71_out), .sel(multiplexer_70_out));
  Multiplexer #(.disabled(0), .enable("false")) multiplexer_72 (
    .in0(1'b0), .in1(multiplexer_57_out), .out(multiplexer_72_out), .sel(in_36));
  Multiplexer #(.disabled(0), .enable("false")) multiplexer_73 (
    .in0(1'b1), .in1(1'b0), .out(multiplexer_73_out), .sel(multiplexer_72_out));
  Multiplexer #(.disabled(0), .enable("false")) multiplexer_74 (
    .in0(1'b0), .in1(multiplexer_59_out), .out(multiplexer_74_out), .sel(in_44));
  Multiplexer #(.disabled(0), .enable("false")) multiplexer_75 (
    .in0(1'b0), .in1(multiplexer_61_out), .out(multiplexer_75_out), .sel(in_44));
  Multiplexer #(.disabled(0), .enable("false")) multiplexer_76 (
    .in0(1'b0), .in1(multiplexer_77_out), .out(multiplexer_76_out), .sel(multiplexer_39_out));
  Multiplexer #(.disabled(0), .enable("false")) multiplexer_77 (
    .in0(1'b0), .in1(multiplexer_63_out), .out(multiplexer_77_out), .sel(multiplexer_36_out));
  Multiplexer #(.disabled(0), .enable("false")) multiplexer_78 (
    .in0(1'b0), .in1(multiplexer_79_out), .out(multiplexer_78_out), .sel(multiplexer_39_out));
  Multiplexer #(.disabled(0), .enable("false")) multiplexer_79 (
    .in0(1'b0), .in1(multiplexer_65_out), .out(multiplexer_79_out), .sel(multiplexer_36_out));
  Multiplexer #(.disabled(0), .enable("false")) multiplexer_80 (
    .in0(1'b1), .in1(1'b0), .out(multiplexer_80_out), .sel(multiplexer_74_out));
  Multiplexer #(.disabled(0), .enable("false")) multiplexer_81 (
    .in0(1'b1), .in1(1'b0), .out(multiplexer_81_out), .sel(multiplexer_75_out));
  Multiplexer #(.disabled(0), .enable("false")) multiplexer_82 (
    .in0(1'b1), .in1(1'b0), .out(multiplexer_82_out), .sel(multiplexer_76_out));
  Multiplexer #(.disabled(0), .enable("false")) multiplexer_83 (
    .in0(1'b1), .in1(1'b0), .out(multiplexer_83_out), .sel(multiplexer_78_out));
  Multiplexer #(.disabled(0), .enable("false")) multiplexer_84 (
    .in0(1'b0), .in1(multiplexer_85_out), .out(multiplexer_84_out), .sel(in_23));
  Multiplexer #(.disabled(0), .enable("false")) multiplexer_85 (
    .in0(1'b0), .in1(multiplexer_89_out), .out(multiplexer_85_out), .sel(multiplexer_67_out));
  Multiplexer #(.disabled(0), .enable("false")) multiplexer_86 (
    .in0(1'b1), .in1(1'b0), .out(multiplexer_86_out), .sel(multiplexer_84_out));
  Multiplexer #(.disabled(0), .enable("false")) multiplexer_87 (
    .in0(1'b0), .in1(multiplexer_88_out), .out(multiplexer_87_out), .sel(in_32));
  Multiplexer #(.disabled(0), .enable("false")) multiplexer_88 (
    .in0(1'b0), .in1(multiplexer_86_out), .out(multiplexer_88_out), .sel(multiplexer_69_out));
  Multiplexer #(.disabled(0), .enable("false")) multiplexer_89 (
    .in0(1'b1), .in1(1'b0), .out(multiplexer_89_out), .sel(multiplexer_87_out));
  Multiplexer #(.disabled(0), .enable("false")) multiplexer_90 (
    .in0(1'b0), .in1(multiplexer_91_out), .out(multiplexer_90_out), .sel(in_33));
  Multiplexer #(.disabled(0), .enable("false")) multiplexer_91 (
    .in0(1'b0), .in1(multiplexer_95_out), .out(multiplexer_91_out), .sel(multiplexer_71_out));
  Multiplexer #(.disabled(0), .enable("false")) multiplexer_92 (
    .in0(1'b1), .in1(1'b0), .out(multiplexer_92_out), .sel(multiplexer_90_out));
  Multiplexer #(.disabled(0), .enable("false")) multiplexer_93 (
    .in0(1'b0), .in1(multiplexer_94_out), .out(multiplexer_93_out), .sel(in_38));
  Multiplexer #(.disabled(0), .enable("false")) multiplexer_94 (
    .in0(1'b0), .in1(multiplexer_92_out), .out(multiplexer_94_out), .sel(multiplexer_73_out));
  Multiplexer #(.disabled(0), .enable("false")) multiplexer_95 (
    .in0(1'b1), .in1(1'b0), .out(multiplexer_95_out), .sel(multiplexer_93_out));
  Multiplexer #(.disabled(0), .enable("false")) multiplexer_96 (
    .in0(1'b0), .in1(multiplexer_97_out), .out(multiplexer_96_out), .sel(in_39));
  Multiplexer #(.disabled(0), .enable("false")) multiplexer_97 (
    .in0(1'b0), .in1(multiplexer_101_out), .out(multiplexer_97_out), .sel(multiplexer_80_out));
  Multiplexer #(.disabled(0), .enable("false")) multiplexer_98 (
    .in0(1'b1), .in1(1'b0), .out(multiplexer_98_out), .sel(multiplexer_96_out));
  Multiplexer #(.disabled(0), .enable("false")) multiplexer_99 (
    .in0(1'b0), .in1(multiplexer_100_out), .out(multiplexer_99_out), .sel(in_48));
  Multiplexer #(.disabled(0), .enable("false")) multiplexer_100 (
    .in0(1'b0), .in1(multiplexer_98_out), .out(multiplexer_100_out), .sel(multiplexer_81_out));
  Multiplexer #(.disabled(0), .enable("false")) multiplexer_101 (
    .in0(1'b1), .in1(1'b0), .out(multiplexer_101_out), .sel(multiplexer_99_out));
  Multiplexer #(.disabled(0), .enable("false")) multiplexer_102 (
    .in0(1'b0), .in1(multiplexer_103_out), .out(multiplexer_102_out), .sel(in_49));
  Multiplexer #(.disabled(0), .enable("false")) multiplexer_103 (
    .in0(1'b0), .in1(multiplexer_107_out), .out(multiplexer_103_out), .sel(multiplexer_82_out));
  Multiplexer #(.disabled(0), .enable("false")) multiplexer_104 (
    .in0(1'b1), .in1(1'b0), .out(multiplexer_104_out), .sel(multiplexer_102_out));
  Multiplexer #(.disabled(0), .enable("false")) multiplexer_105 (
    .in0(1'b0), .in1(multiplexer_106_out), .out(multiplexer_105_out), .sel(in_58));
  Multiplexer #(.disabled(0), .enable("false")) multiplexer_106 (
    .in0(1'b0), .in1(multiplexer_104_out), .out(multiplexer_106_out), .sel(multiplexer_83_out));
  Multiplexer #(.disabled(0), .enable("false")) multiplexer_107 (
    .in0(1'b1), .in1(1'b0), .out(multiplexer_107_out), .sel(multiplexer_105_out));

  // Notes on the sheet:
  //   И-НЕ на 2 элемента
  //   И-НЕ на 3 элемента
  //   двухступ RS
  //   НЕ
  //   асинхр RS
  //   синхр RS
  //   T пер фронт
  //   JK с инв (пер фронт)
  //   JK без инв (зад фронт)
endmodule
