// Logisim project sixthcirc.circ as structural Verilog: 1 circuit, main circuit main
module main (
);

  wire button_1_out, button_2_out, button_3_out, C, e5, main_1_p1, main_1_p2, nand_1_out, nand_2_out,
       nand_3_out, nand_4_out, nand_5_out, nand_6_out, nand_7_out, nand_8_out, nand_9_out, nand_10_out,
       nand_11_out, nand_12_out, nand_13_out, nand_14_out, nand_15_out, nand_16_out, nand_17_out, nor_1_out,
       nor_2_out, nor_3_out, nor_4_out, nor_5_out, nor_6_out, nor_7_out, nor_8_out, nor_9_out, nor_10_out,
       nor_11_out, nor_12_out, nor_13_out, nor_14_out, nor_15_out, nor_16_out, nor_17_out, nor_18_out,
       undriven, undriven_2, undriven_3, undriven_4, undriven_5, undriven_6, undriven_7, undriven_8,
       undriven_9, undriven_10, undriven_11, undriven_12;
  wire [2:0] co;
  wire [3:0] Fi, n0, n1, n2, n3, n4, S1, S2, S3;
  wire [15:0] d1, d2, d3, d4, e1, e2, e3, e4;
  wire [19:0] _1i, _2i, _3i, _4i, _5i, _6i, _7i, _8i, _9i;
  wire [29:0] _1, _2, _3, _4, _5, _6, _7, _8, _9, _10, _11, _12, _13, _14, _15, _16, _17, _18, _19, _20;

  DotMatrix #(.matrixcols(6), .matrixrows(5)) dotmatrix_1 (
    .col0(_20[29:25]), .col1(_20[24:20]), .col2(_20[19:15]), .col3(_20[14:10]), .col4(_20[9:5]),
    .col5(_20[4:0]));
  DotMatrix #(.matrixcols(6), .matrixrows(5)) dotmatrix_2 (
    .col0(_15[29:25]), .col1(_15[24:20]), .col2(_15[19:15]), .col3(_15[14:10]), .col4(_15[9:5]),
    .col5(_15[4:0]));
  nor nor_1 (nor_1_out, Fi[3], Fi[3]);
  nand nand_1 (nand_1_out, undriven, undriven);
  nand nand_2 (nand_2_out, undriven_2, undriven_2);
  DotMatrix #(.matrixcols(6), .matrixrows(5)) dotmatrix_3 (
    .col0(_16[29:25]), .col1(_16[24:20]), .col2(_16[19:15]), .col3(_16[14:10]), .col4(_16[9:5]),
    .col5(_16[4:0]));
  Hex_Digit_Display hex_digit_display_1 (.value(d1[11:8]));  // open: dp
  Hex_Digit_Display hex_digit_display_2 (.value(d1[15:12]));  // open: dp
  nor nor_2 (nor_2_out, Fi[1], Fi[1]);
  nor nor_3 (nor_3_out, Fi[2], Fi[2]);
  nand nand_3 (nand_3_out, undriven_4, undriven_4);
  nand nand_4 (nand_4_out, undriven_6, undriven_6);
  nand nand_5 (nand_5_out, undriven_5, undriven_5);
  nand nand_6 (nand_6_out, undriven_3, undriven_3);
  DotMatrix #(.matrixcols(6), .matrixrows(5)) dotmatrix_4 (
    .col0(_17[29:25]), .col1(_17[24:20]), .col2(_17[19:15]), .col3(_17[14:10]), .col4(_17[9:5]),
    .col5(_17[4:0]));
  Hex_Digit_Display hex_digit_display_3 (.value(d1[3:0]));  // open: dp
  Hex_Digit_Display hex_digit_display_4 (.value(d1[7:4]));  // open: dp
  nor nor_4 (nor_4_out, Fi[0], Fi[0]);
  nand nand_7 (nand_7_out, undriven_7, undriven_7);
  nand nand_8 (nand_8_out, undriven_8, undriven_8);
  DotMatrix #(.matrixcols(6), .matrixrows(5)) dotmatrix_5 (
    .col0(_18[29:25]), .col1(_18[24:20]), .col2(_18[19:15]), .col3(_18[14:10]), .col4(_18[9:5]),
    .col5(_18[4:0]));
  DotMatrix #(.matrixcols(6), .matrixrows(5)) dotmatrix_6 (
    .col0(_19[29:25]), .col1(_19[24:20]), .col2(_19[19:15]), .col3(_19[14:10]), .col4(_19[9:5]),
    .col5(_19[4:0]));
  Hex_Digit_Display hex_digit_display_5 (.value(d2[15:12]));  // open: dp
  Hex_Digit_Display hex_digit_display_6 (.value(d2[11:8]));  // open: dp
  DotMatrix #(.matrixcols(6), .matrixrows(5)) dotmatrix_7 (
    .col0(_2[29:25]), .col1(_2[24:20]), .col2(_2[19:15]), .col3(_2[14:10]), .col4(_2[9:5]), .col5(_2[4:0]));
  DotMatrix #(.matrixcols(6), .matrixrows(5)) dotmatrix_8 (
    .col0(_1[29:25]), .col1(_1[24:20]), .col2(_1[19:15]), .col3(_1[14:10]), .col4(_1[9:5]), .col5(_1[4:0]));
  Hex_Digit_Display hex_digit_display_7 (.value(d2[3:0]));  // open: dp
  Hex_Digit_Display hex_digit_display_8 (.value(d2[7:4]));  // open: dp
  nor nor_5 (nor_5_out, Fi[2], Fi[1], nor_4_out);
  nor nor_6 (nor_6_out, nor_1_out, Fi[2], Fi[0]);
  nor nor_7 (nor_7_out, nor_1_out, nor_2_out, Fi[0]);
  nor nor_8 (nor_8_out, Fi[3], nor_3_out, nor_2_out, nor_4_out);
  nand nand_9 (nand_9_out, nand_6_out, nand_5_out, undriven_8);
  nand nand_10 (nand_10_out, undriven_2, nand_6_out, nand_8_out);
  nand nand_11 (nand_11_out, undriven_2, undriven_5, nand_8_out);
  nand nand_12 (nand_12_out, nand_2_out, undriven_3, undriven_5, undriven_8);
  DotMatrix #(.matrixcols(6), .matrixrows(5)) dotmatrix_9 (
    .col0(_3[29:25]), .col1(_3[24:20]), .col2(_3[19:15]), .col3(_3[14:10]), .col4(_3[9:5]), .col5(_3[4:0]));
  nand nand_13 (nand_13_out, undriven_4, nand_4_out);
  nand nand_14 (nand_14_out, nand_1_out, nand_7_out);
  nand nand_15 (nand_15_out, nand_1_out, nand_3_out, undriven_6);
  nand nand_16 (nand_16_out, undriven, undriven_6, undriven_7);
  nand nand_17 (nand_17_out, nand_9_out, nand_10_out, nand_11_out, nand_12_out);
  DotMatrix #(.matrixcols(6), .matrixrows(5)) dotmatrix_10 (
    .col0(_4[29:25]), .col1(_4[24:20]), .col2(_4[19:15]), .col3(_4[14:10]), .col4(_4[9:5]), .col5(_4[4:0]));
  Hex_Digit_Display hex_digit_display_9 (.value(d3[15:12]));  // open: dp
  nor nor_9 (nor_9_out, nor_5_out, nor_6_out, nor_7_out, nor_8_out);
  // NAND_Gate nand_18 has open pins: in0=nand_17_out, in1=nand_17_out, out=open
  DotMatrix #(.matrixcols(6), .matrixrows(5)) dotmatrix_11 (
    .col0(_6[29:25]), .col1(_6[24:20]), .col2(_6[19:15]), .col3(_6[14:10]), .col4(_6[9:5]), .col5(_6[4:0]));
  DotMatrix #(.matrixcols(6), .matrixrows(5)) dotmatrix_12 (
    .col0(_5[29:25]), .col1(_5[24:20]), .col2(_5[19:15]), .col3(_5[14:10]), .col4(_5[9:5]), .col5(_5[4:0]));
  Hex_Digit_Display hex_digit_display_10 (.value(d3[7:4]));  // open: dp
  Hex_Digit_Display hex_digit_display_11 (.value(d3[11:8]));  // open: dp
  // NAND_Gate nand_19 has open pins: in0=nand_13_out, in1=nand_14_out, in2=nand_15_out, in3=nand_16_out, out=open
  DotMatrix #(.matrixcols(6), .matrixrows(5)) dotmatrix_13 (
    .col0(_7[29:25]), .col1(_7[24:20]), .col2(_7[19:15]), .col3(_7[14:10]), .col4(_7[9:5]), .col5(_7[4:0]));
  Hex_Digit_Display hex_digit_display_12 (.value(d3[3:0]));  // open: dp
  nor nor_10 (nor_10_out, undriven_9, undriven_9);
  DotMatrix #(.matrixcols(6), .matrixrows(5)) dotmatrix_14 (
    .col0(_8[29:25]), .col1(_8[24:20]), .col2(_8[19:15]), .col3(_8[14:10]), .col4(_8[9:5]), .col5(_8[4:0]));
  Hex_Digit_Display hex_digit_display_13 (.value(d4[15:12]));  // open: dp
  LED \u_Ошибочный_код  (.in(e5));
  nor nor_11 (nor_11_out, undriven_11, undriven_11);
  nor nor_12 (nor_12_out, undriven_10, undriven_10);
  DotMatrix #(.matrixcols(6), .matrixrows(5)) dotmatrix_15 (
    .col0(_10[29:25]), .col1(_10[24:20]), .col2(_10[19:15]), .col3(_10[14:10]), .col4(_10[9:5]),
    .col5(_10[4:0]));
  DotMatrix #(.matrixcols(6), .matrixrows(5)) dotmatrix_16 (
    .col0(_9[29:25]), .col1(_9[24:20]), .col2(_9[19:15]), .col3(_9[14:10]), .col4(_9[9:5]), .col5(_9[4:0]));
  Hex_Digit_Display hex_digit_display_14 (.value(d4[7:4]));  // open: dp
  Hex_Digit_Display hex_digit_display_15 (.value(d4[11:8]));  // open: dp
  nor nor_13 (nor_13_out, undriven_12, undriven_12);
  DotMatrix #(.matrixcols(6), .matrixrows(5)) dotmatrix_17 (
    .col0(_11[29:25]), .col1(_11[24:20]), .col2(_11[19:15]), .col3(_11[14:10]), .col4(_11[9:5]),
    .col5(_11[4:0]));
  Hex_Digit_Display hex_digit_display_16 (.value(d4[3:0]));  // open: dp
  DotMatrix #(.matrixcols(4), .matrixrows(5)) dotmatrix_18 (
    .col0(_8i[19:15]), .col1(_8i[14:10]), .col2(_8i[9:5]), .col3(_8i[4:0]));
  DotMatrix #(.matrixcols(4), .matrixrows(5)) dotmatrix_19 (
    .col0(_9i[19:15]), .col1(_9i[14:10]), .col2(_9i[9:5]), .col3(_9i[4:0]));
  Button button_1 (.out(button_1_out));
  Button button_2 (.out(button_2_out));
  Button button_3 (.out(button_3_out));
  Hex_Digit_Display hex_digit_display_17 (.value(n4));  // open: dp
  DotMatrix #(.matrixcols(6), .matrixrows(5)) dotmatrix_20 (
    .col0(_12[29:25]), .col1(_12[24:20]), .col2(_12[19:15]), .col3(_12[14:10]), .col4(_12[9:5]),
    .col5(_12[4:0]));
  Hex_Digit_Display hex_digit_display_18 (.value(S1));  // open: dp
  Hex_Digit_Display hex_digit_display_19 (.value(S2));  // open: dp
  DotMatrix #(.matrixcols(4), .matrixrows(5)) dotmatrix_21 (
    .col0(_7i[19:15]), .col1(_7i[14:10]), .col2(_7i[9:5]), .col3(_7i[4:0]));
  DotMatrix #(.matrixcols(4), .matrixrows(5)) dotmatrix_22 (
    .col0(_6i[19:15]), .col1(_6i[14:10]), .col2(_6i[9:5]), .col3(_6i[4:0]));
  Hex_Digit_Display hex_digit_display_20 (.value(n3));  // open: dp
  Hex_Digit_Display hex_digit_display_21 (.value(n2));  // open: dp
  DotMatrix #(.matrixcols(6), .matrixrows(5)) dotmatrix_23 (
    .col0(_13[29:25]), .col1(_13[24:20]), .col2(_13[19:15]), .col3(_13[14:10]), .col4(_13[9:5]),
    .col5(_13[4:0]));
  Hex_Digit_Display hex_digit_display_22 (.value(S3));  // open: dp
  DotMatrix #(.matrixcols(4), .matrixrows(5)) dotmatrix_24 (
    .col0(_5i[19:15]), .col1(_5i[14:10]), .col2(_5i[9:5]), .col3(_5i[4:0]));
  DotMatrix #(.matrixcols(4), .matrixrows(5)) dotmatrix_25 (
    .col0(_4i[19:15]), .col1(_4i[14:10]), .col2(_4i[9:5]), .col3(_4i[4:0]));
  // mainCore_main main_1: pin names not known; wires that end beside it: main_1_p1, main_1_p2, nor_9_out, main_1_p1, main_1_p2, button_1_out, button_2_out, button_3_out, 20'ha018, e5, S2, C, S3, S1, n4, n2, n3, e1, n1, e2, n0, e3, _15, e4, _16, co, _17, Fi, _18, d1, _19, d2, _20, d3, _14, d4, _13, _1, _2, _3, _4, _5, _6, _7, _8, _9, _10, _11, _12
  nor nor_14 (nor_14_out, nor_12_out, undriven_11);
  nor nor_15 (nor_15_out, undriven_9, undriven_12);
  nor nor_16 (nor_16_out, undriven_9, undriven_10, nor_11_out);
  nor nor_17 (nor_17_out, nor_10_out, nor_11_out, nor_13_out);
  Hex_Digit_Display hex_digit_display_23 (.value(n1));  // open: dp
  Hex_Digit_Display hex_digit_display_24 (.value(n0));  // open: dp
  DotMatrix #(.matrixcols(6), .matrixrows(5)) dotmatrix_26 (
    .col0(_14[29:25]), .col1(_14[24:20]), .col2(_14[19:15]), .col3(_14[14:10]), .col4(_14[9:5]),
    .col5(_14[4:0]));
  DotMatrix #(.matrixcols(4), .matrixrows(5)) dotmatrix_27 (
    .col0(_3i[19:15]), .col1(_3i[14:10]), .col2(_3i[9:5]), .col3(_3i[4:0]));
  DotMatrix #(.matrixcols(4), .matrixrows(5)) dotmatrix_28 (
    .col0(_2i[19:15]), .col1(_2i[14:10]), .col2(_2i[9:5]), .col3(_2i[4:0]));
  nor nor_18 (nor_18_out, nor_14_out, nor_15_out, nor_16_out, nor_17_out);
  DotMatrix #(.matrixcols(4), .matrixrows(5)) dotmatrix_29 (
    .col0(_1i[19:15]), .col1(_1i[14:10]), .col2(_1i[9:5]), .col3(_1i[4:0]));
  // NOR_Gate nor_19 has open pins: in0=nor_18_out, in1=nor_18_out, out=open
  LED led_1 (.in(e3[15]));
  LED led_2 (.in(e3[14]));
  LED led_3 (.in(e3[13]));
  LED led_4 (.in(e3[12]));
  LED led_5 (.in(e3[11]));
  LED led_6 (.in(e3[10]));
  LED led_7 (.in(e3[9]));
  LED led_8 (.in(e3[8]));
  LED led_9 (.in(e3[7]));
  LED led_10 (.in(e3[6]));
  LED led_11 (.in(e3[5]));
  LED led_12 (.in(e3[4]));
  LED led_13 (.in(e3[3]));
  LED led_14 (.in(e3[2]));
  LED led_15 (.in(e3[1]));
  LED led_16 (.in(e3[0]));
  LED led_17 (.in(e1[15]));
  LED led_18 (.in(e1[14]));
  LED led_19 (.in(e1[13]));
  LED led_20 (.in(e1[12]));
  LED led_21 (.in(e1[11]));
  LED led_22 (.in(e1[10]));
  LED led_23 (.in(e1[9]));
  LED led_24 (.in(e1[8]));
  LED led_25 (.in(e1[7]));
  LED led_26 (.in(e1[6]));
  LED led_27 (.in(e1[5]));
  LED led_28 (.in(e1[4]));
  LED led_29 (.in(e1[3]));
  LED led_30 (.in(e1[2]));
  LED led_31 (.in(e1[1]));
  LED led_32 (.in(e1[0]));
  LED led_33 (.in(e4[15]));
  LED led_34 (.in(e4[14]));
  LED led_35 (.in(e4[13]));
  LED led_36 (.in(e4[12]));
  LED led_37 (.in(e4[11]));
  LED led_38 (.in(e4[10]));
  LED led_39 (.in(e4[9]));
  LED led_40 (.in(e4[8]));
  LED led_41 (.in(e4[7]));
  LED led_42 (.in(e4[6]));
  LED led_43 (.in(e4[5]));
  LED led_44 (.in(e4[4]));
  LED led_45 (.in(e4[3]));
  LED led_46 (.in(e4[2]));
  LED led_47 (.in(e4[1]));
  LED led_48 (.in(e4[0]));
  LED led_49 (.in(e2[15]));
  LED led_50 (.in(e2[14]));
  LED led_51 (.in(e2[13]));
  LED led_52 (.in(e2[12]));
  LED led_53 (.in(e2[11]));
  LED led_54 (.in(e2[10]));
  LED led_55 (.in(e2[9]));
  LED led_56 (.in(e2[8]));
  LED led_57 (.in(e2[7]));
  LED led_58 (.in(e2[6]));
  LED led_59 (.in(e2[5]));
  LED led_60 (.in(e2[4]));
  LED led_61 (.in(e2[3]));
  LED led_62 (.in(e2[2]));
  LED led_63 (.in(e2[1]));
  LED led_64 (.in(e2[0]));
  // prav_main main_2: pin names not known; wires that end beside it: co, _1i, _9i, _2i, _8i, _3i, _7i, _4i, _6i, _5i

  // Notes on the sheet:
  //   F1:
  //   Группа
  //   Исходные данные:
  //   МКНФ и-не
  //   МКНФ или-не
  //   МДНФ и-не
  //   F2:
  //   Студент
  //   F3:
  //   F4:
  //   МДНФ или-не
  //   Личный код:
  //   CNT:
  //   Напр.
  //   Макс.
  //   Шаг
  //   .
  //   Напр.: 0 - сложение
  //   1 - вычитание
  //   Макс. - максимальное
  //   значение счетчика
  //   .
  //   Ошибки в F3
  //   Ошибки в F1
  //   0000
  //   0001
  //   0010
  //   0011
  //   0100
  //   0101
  //   0110
  //   0111
  //   1000
  //   1001
  //   1010
  //   1011
  //   1100
  //   1101
  //   1110
  //   1111
  //   0000
  //   0001
  //   0010
  //   0011
  //   0100
  //   0101
  //   0110
  //   0111
  //   1000
  //   1001
  //   1010
  //   1011
  //   1100
  //   1101
  //   1110
  //   1111
  //   Ошибки в F4
  //   Ошибки в  F2
  //   0000
  //   0001
  //   0010
  //   0011
  //   0100
  //   0101
  //   0110
  //   0111
  //   1000
  //   1001
  //   1010
  //   1011
  //   1100
  //   1101
  //   1110
  //   1111
  //   0000
  //   0001
  //   0010
  //   0011
  //   0100
  //   0101
  //   0110
  //   0111
  //   1000
  //   1001
  //   1010
  //   1011
  //   1100
  //   1101
  //   1110
  //   1111
endmodule
