// Logisim project trig.circ as structural Verilog: 1 circuit, main circuit main
module main (
  input  nS,
  input  nR,
  input  S,
  input  R,
  input  S_2,
  input  C,
  input  R_2,
  input  nS_2,
  input  S_3,
  input  C_2,
  input  R_3,
  input  nR_2,
  input  D,
  input  C_3,
  input  nS_3,
  input  nR_3,
  input  nS_4,
  input  nR_4,
  input  nS_5,
  input  T,
  input  nR_5,
  input  nS_6,
  input  J,
  input  C_4,
  input  K,
  input  nR_6
);

  wire clock_1_out, clock_2_out, nand_1_out, nand_2_out, nand_3_out, nand_4_out, nand_5_out, nand_6_out,
       nand_7_out, nand_8_out, nand_9_out, nand_10_out, nand_11_out, nand_12_out, nand_13_out, nand_14_out,
       nand_15_out, nand_16_out, nand_17_out, nand_18_out, nand_19_out, nand_20_out, nand_21_out,
       nand_22_out, nand_23_out, nand_24_out, nand_25_out, nand_26_out, nand_27_out, nand_28_out,
       nand_29_out, nand_30_out, nand_31_out, nand_32_out, nand_33_out, nand_34_out, nand_35_out,
       nand_36_out, nand_37_out, nand_38_out, nand_39_out, nand_40_out, nand_41_out, nand_42_out,
       nand_43_out, nor_1_out, nor_2_out, nor_3_out, nor_4_out, nor_5_out, nor_6_out, nor_7_out, nor_8_out;

  nand nand_1 (nand_1_out, C_2, C_2);
  Clock clock_1 (.out(clock_1_out));
  Clock clock_2 (.out(clock_2_out));
  nand nand_2 (nand_2_out, T, T);
  nand nand_3 (nand_3_out, nS, nand_4_out);
  nand nand_4 (nand_4_out, nand_3_out, nR);
  nor nor_1 (nor_1_out, S, nor_2_out);
  nor nor_2 (nor_2_out, nor_1_out, R);
  nand nand_5 (nand_5_out, S_2, C);
  nand nand_6 (nand_6_out, C, R_2);
  nand nand_7 (nand_7_out, S_3, nand_1_out);
  nand nand_8 (nand_8_out, nand_1_out, R_3);
  nand nand_9 (nand_9_out, D, D);
  nand nand_10 (nand_10_out, nand_9_out, C_3);
  nand nand_11 (nand_11_out, C_3, D);
  nand nand_12 (nand_12_out, nS_3, nand_22_out);
  nand nand_13 (nand_13_out, nand_23_out, nR_3);
  nor nor_3 (nor_3_out, nS_4, nor_5_out);
  nor nor_4 (nor_4_out, nor_6_out, nR_4);
  nand nand_14 (nand_14_out, nand_39_out, nand_2_out);
  nand nand_15 (nand_15_out, nand_2_out, nand_38_out);
  nand nand_16 (nand_16_out, nand_43_out, J, C_4);
  nand nand_17 (nand_17_out, C_4, K, nand_41_out);
  LED led_1 (.in(nand_3_out));
  LED led_2 (.in(nand_4_out));
  LED led_3 (.in(nor_1_out));
  LED led_4 (.in(nor_2_out));
  nand nand_18 (nand_18_out, nand_5_out, nand_19_out);
  nand nand_19 (nand_19_out, nand_18_out, nand_6_out);
  nand nand_20 (nand_20_out, nS_2, nand_7_out, nand_21_out);
  nand nand_21 (nand_21_out, nand_20_out, nand_8_out, nR_2);
  nand nand_22 (nand_22_out, clock_1_out, nand_12_out, nand_23_out);
  nand nand_23 (nand_23_out, nand_22_out, nand_13_out, clock_1_out);
  nor nor_5 (nor_5_out, clock_2_out, nor_3_out, nor_6_out);
  nor nor_6 (nor_6_out, nor_5_out, nor_4_out, clock_2_out);
  nand nand_24 (nand_24_out, nS_5, nand_14_out, nand_25_out);
  nand nand_25 (nand_25_out, nand_24_out, nand_15_out, nR_5);
  nand nand_26 (nand_26_out, nS_6, nand_16_out, nand_27_out);
  nand nand_27 (nand_27_out, nand_26_out, nand_17_out, nR_6);
  LED led_5 (.in(nand_18_out));
  LED led_6 (.in(nand_19_out));
  nand nand_28 (nand_28_out, nand_20_out, C_2);
  nand nand_29 (nand_29_out, C_2, nand_21_out);
  nand nand_30 (nand_30_out, nand_10_out, nand_31_out);
  nand nand_31 (nand_31_out, nand_30_out, nand_11_out);
  nand nand_32 (nand_32_out, nand_22_out, nand_33_out);
  nand nand_33 (nand_33_out, nand_32_out, nand_23_out);
  nor nor_7 (nor_7_out, nor_5_out, nor_8_out);
  nor nor_8 (nor_8_out, nor_7_out, nor_6_out);
  nand nand_34 (nand_34_out, nand_24_out, T);
  nand nand_35 (nand_35_out, T, nand_25_out);
  nand nand_36 (nand_36_out, nS_2, nand_28_out, nand_37_out);
  nand nand_37 (nand_37_out, nand_36_out, nand_29_out, nR_2);
  LED led_7 (.in(nand_30_out));
  LED led_8 (.in(nand_31_out));
  LED led_9 (.in(nand_32_out));
  LED led_10 (.in(nand_33_out));
  LED led_11 (.in(nor_7_out));
  LED led_12 (.in(nor_8_out));
  nand nand_38 (nand_38_out, nS_5, nand_34_out, nand_39_out);
  nand nand_39 (nand_39_out, nand_38_out, nand_35_out, nR_5);
  nand nand_40 (nand_40_out, nand_26_out, nand_17_out, nand_16_out);
  nand nand_41 (nand_41_out, nS_6, nand_40_out, nand_43_out);
  nand nand_42 (nand_42_out, nand_16_out, nand_17_out, nand_27_out);
  nand nand_43 (nand_43_out, nand_41_out, nand_42_out, nR_6);
  LED led_13 (.in(nand_36_out));
  LED led_14 (.in(nand_37_out));
  LED led_15 (.in(nand_38_out));
  LED led_16 (.in(nand_39_out));
  LED led_17 (.in(nand_41_out));
  LED led_18 (.in(nand_43_out));

  // Notes on the sheet:
  //   Q
  //   !Q
  //   !Q
  //   Q
  //   Q
  //   !Q
  //   !Q
  //   Q
  //   Q
  //   !Q
  //   Q
  //   !Q
  //   Q
  //   !Q
  //   Q
  //   !Q
  //   Q
  //   !Q
endmodule
